// Logisim project Door.circ as structural Verilog: 1 circuit, main circuit main
module main (
  input  CLK,
  input  Sclose,
  input  Sopen,
  input  Psensor,
  output On
);

  wire pld_1_p3, pld_1_p12, pld_1_p14, pld_1_p15, pld_1_p16, pld_1_p17, pld_1_p18, usbport_1_p1,
       usbport_1_p2, usbport_1_p3, usbport_1_p4, usbport_1_p5;

  // UsbPort usbport_1: pin names not known; wires that end beside it: usbport_1_p1, usbport_1_p2, usbport_1_p3, usbport_1_p4, usbport_1_p5
  // PLD #(.Contents("{\"version\":\"1.0\",\"deviceId\":\"v750c\",\"file\":\"template.doc\",\"variables\":{},\"productTerms\":[{\"type\":\"M\",\"pin\":25,\"name\":\"C0.d\",\"expression\":\"C0\\u0026!C1\\u0026!C2\\u0026!R0#!C0\\u0026!C1\\u0026C2\\u0026Sopen#!C0\\u0026!C1\\u0026!C2\\u0026Wr#C0\\u0026C1\\u0026!C2\\u0026!Psensor\\u0026!Sclose\"},{\"type\":\"M\",\"pin\":25,\"name\":\"C0.ar\",\"expression\":\"0\"},{\"type\":\"M\",\"pin\":25,\"name\":\"C0.ck\",\"expression\":\"CLK\"},{\"type\":\"M\",\"pin\":25,\"name\":\"C0.sp\",\"expression\":\"0\"},{\"type\":\"M\",\"pin\":26,\"name\":\"C1.d\",\"expression\":\"C0\\u0026!C1\\u0026!C2#C0\\u0026!C2\\u0026!Psensor\\u0026!Sclose#!C0\\u0026!C1\\u0026C2\\u0026Sopen#!C0\\u0026C1\\u0026!C2\\u0026!Sopen\"},{\"type\":\"M\",\"pin\":26,\"name\":\"C1.ar\",\"expression\":\"0\"},{\"type\":\"M\",\"pin\":26,\"name\":\"C1.ck\",\"expression\":\"CLK\"},{\"type\":\"M\",\"pin\":26,\"name\":\"C1.sp\",\"expression\":\"0\"},{\"type\":\"M\",\"pin\":27,\"name\":\"C2.d\",\"expression\":\"C0\\u0026C1\\u0026!C2\\u0026Psensor#!C0\\u0026!C1\\u0026C2\\u0026!Sopen\"},{\"type\":\"M\",\"pin\":27,\"name\":\"C2.ar\",\"expression\":\"0\"},{\"type\":\"M\",\"pin\":27,\"name\":\"C2.ck\",\"expression\":\"CLK\"},{\"type\":\"M\",\"pin\":27,\"name\":\"C2.sp\",\"expression\":\"0\"},{\"type\":\"V\",\"pin\":15,\"name\":\"Dout0\",\"expression\":\"R0#!C0\\u0026!C1\\u0026C2#!C0\\u0026C1\\u0026!C2\"},{\"type\":\"V\",\"pin\":16,\"name\":\"Dout1\",\"expression\":\"R1\"},{\"type\":\"V\",\"pin\":17,\"name\":\"Dout2\",\"expression\":\"R2\"},{\"type\":\"V\",\"pin\":18,\"name\":\"Dout3\",\"expression\":\"R3\"},{\"type\":\"V\",\"pin\":19,\"name\":\"Dout4\",\"expression\":\"R4\"},{\"type\":\"V\",\"pin\":20,\"name\":\"On\",\"expression\":\"C0\\u0026!C2#C1\\u0026!C2#!C0\\u0026!C1\\u0026C2\"},{\"type\":\"M\",\"pin\":28,\"name\":\"R0.d\",\"expression\":\"Din0\"},{\"type\":\"M\",\"pin\":28,\"name\":\"R0.ar\",\"expression\":\"0\"},{\"type\":\"M\",\"pin\":28,\"name\":\"R0.ck\",\"expression\":\"busy\"},{\"type\":\"M\",\"pin\":28,\"name\":\"R0.sp\",\"expression\":\"0\"},{\"type\":\"M\",\"pin\":29,\"name\":\"R1.d\",\"expression\":\"Din1\"},{\"type\":\"M\",\"pin\":29,\"name\":\"R1.ar\",\"expression\":\"0\"},{\"type\":\"M\",\"pin\":29,\"name\":\"R1.ck\",\"expression\":\"busy\"},{\"type\":\"M\",\"pin\":29,\"name\":\"R1.sp\",\"expression\":\"0\"},{\"type\":\"M\",\"pin\":30,\"name\":\"R2.d\",\"expression\":\"Din2\"},{\"type\":\"M\",\"pin\":30,\"name\":\"R2.ar\",\"expression\":\"0\"},{\"type\":\"M\",\"pin\":30,\"name\":\"R2.ck\",\"expression\":\"busy\"},{\"type\":\"M\",\"pin\":30,\"name\":\"R2.sp\",\"expression\":\"0\"},{\"type\":\"M\",\"pin\":31,\"name\":\"R3.d\",\"expression\":\"Din3\"},{\"type\":\"M\",\"pin\":31,\"name\":\"R3.ar\",\"expression\":\"0\"},{\"type\":\"M\",\"pin\":31,\"name\":\"R3.ck\",\"expression\":\"busy\"},{\"type\":\"M\",\"pin\":31,\"name\":\"R3.sp\",\"expression\":\"0\"},{\"type\":\"M\",\"pin\":32,\"name\":\"R4.d\",\"expression\":\"Din4\"},{\"type\":\"M\",\"pin\":32,\"name\":\"R4.ar\",\"expression\":\"0\"},{\"type\":\"M\",\"pin\":32,\"name\":\"R4.ck\",\"expression\":\"busy\"},{\"type\":\"M\",\"pin\":32,\"name\":\"R4.sp\",\"expression\":\"0\"},{\"type\":\"I\",\"pin\":0,\"name\":\"T\",\"expression\":\"!C0\\u0026C1\\u0026!C2#!C0\\u0026!C1\\u0026C2\"},{\"type\":\"V\",\"pin\":23,\"name\":\"busy\",\"expression\":\"C0\\u0026!C2#C1\\u0026!C2#!C0\\u0026!C1\\u0026C2\"},{\"type\":\"D\",\"pin\":15,\"name\":\"Dout0.oe\",\"expression\":\"1\"},{\"type\":\"D\",\"pin\":16,\"name\":\"Dout1.oe\",\"expression\":\"1\"},{\"type\":\"D\",\"pin\":17,\"name\":\"Dout2.oe\",\"expression\":\"1\"},{\"type\":\"D\",\"pin\":18,\"name\":\"Dout3.oe\",\"expression\":\"1\"},{\"type\":\"D\",\"pin\":19,\"name\":\"Dout4.oe\",\"expression\":\"1\"},{\"type\":\"D\",\"pin\":20,\"name\":\"On.oe\",\"expression\":\"1\"},{\"type\":\"D\",\"pin\":23,\"name\":\"busy.oe\",\"expression\":\"1\"}],\"projectName\":\"template\",\"pins\":{\"1\":{\"termUsed\":\"-\",\"type\":\"V\",\"name\":\"CLK\",\"number\":1,\"negated\":false,\"extensions\":{},\"fuseNot\":false},\"2\":{\"termUsed\":\"-\",\"type\":\"V\",\"name\":\"Wr\",\"number\":2,\"negated\":false,\"extensions\":{},\"fuseNot\":false},\"3\":{\"termUsed\":\"-\",\"type\":\"V\",\"name\":\"Din0\",\"number\":3,\"negated\":false,\"extensions\":{},\"fuseNot\":false},\"4\":{\"termUsed\":\"-\",\"type\":\"V\",\"name\":\"Din1\",\"number\":4,\"negated\":false,\"extensions\":{},\"fuseNot\":false},\"5\":{\"termUsed\":\"-\",\"type\":\"V\",\"name\":\"Din2\",\"number\":5,\"negated\":false,\"extensions\":{},\"fuseNot\":false},\"6\":{\"termUsed\":\"-\",\"type\":\"V\",\"name\":\"Din3\",\"number\":6,\"negated\":false,\"extensions\":{},\"fuseNot\":false},\"7\":{\"termUsed\":\"-\",\"type\":\"V\",\"name\":\"Din4\",\"number\":7,\"negated\":false,\"extensions\":{},\"fuseNot\":false},\"8\":{\"termUsed\":\"-\",\"type\":\"V\",\"name\":\"Sclose\",\"number\":8,\"negated\":false,\"extensions\":{},\"fuseNot\":false},\"9\":{\"termUsed\":\"-\",\"type\":\"V\",\"name\":\"Sopen\",\"number\":9,\"negated\":false,\"extensions\":{},\"fuseNot\":false},\"10\":{\"termUsed\":\"-\",\"type\":\"V\",\"name\":\"Psensor\",\"number\":10,\"negated\":false,\"extensions\":{},\"fuseNot\":false},\"15\":{\"termUsed\":\"3\",\"type\":\"V\",\"name\":\"Dout0\",\"number\":15,\"negated\":false,\"extensions\":{\"oe\":false},\"fuseNot\":false},\"16\":{\"termUsed\":\"1\",\"type\":\"V\",\"name\":\"Dout1\",\"number\":16,\"negated\":false,\"extensions\":{\"oe\":false},\"fuseNot\":false},\"17\":{\"termUsed\":\"1\",\"type\":\"V\",\"name\":\"Dout2\",\"number\":17,\"negated\":false,\"extensions\":{\"oe\":false},\"fuseNot\":false},\"18\":{\"termUsed\":\"1\",\"type\":\"V\",\"name\":\"Dout3\",\"number\":18,\"negated\":false,\"extensions\":{\"oe\":false},\"fuseNot\":false},\"19\":{\"termUsed\":\"1\",\"type\":\"V\",\"name\":\"Dout4\",\"number\":19,\"negated\":false,\"extensions\":{\"oe\":false},\"fuseNot\":false},\"20\":{\"termUsed\":\"3\",\"type\":\"V\",\"name\":\"On\",\"number\":20,\"negated\":false,\"extensions\":{\"oe\":false},\"fuseNot\":false},\"23\":{\"termUsed\":\"3\",\"type\":\"V\",\"name\":\"busy\",\"number\":23,\"negated\":false,\"extensions\":{\"oe\":false},\"fuseNot\":false},\"25\":{\"termUsed\":\"-\",\"type\":\"N\",\"name\":\"C0\",\"number\":25,\"negated\":false,\"extensions\":{\"ar\":false,\"d\":false,\"ck\":false,\"sp\":false},\"fuseNot\":false},\"26\":{\"termUsed\":\"-\",\"type\":\"N\",\"name\":\"C1\",\"number\":26,\"negated\":false,\"extensions\":{\"ar\":false,\"d\":false,\"ck\":false,\"sp\":false},\"fuseNot\":false},\"27\":{\"termUsed\":\"-\",\"type\":\"N\",\"name\":\"C2\",\"number\":27,\"negated\":false,\"extensions\":{\"ar\":false,\"d\":false,\"ck\":false,\"sp\":false},\"fuseNot\":false},\"28\":{\"termUsed\":\"-\",\"type\":\"N\",\"name\":\"R0\",\"number\":28,\"negated\":false,\"extensions\":{\"ar\":false,\"d\":false,\"ck\":false,\"sp\":false},\"fuseNot\":false},\"29\":{\"termUsed\":\"-\",\"type\":\"N\",\"name\":\"R1\",\"number\":29,\"negated\":false,\"extensions\":{\"ar\":false,\"d\":false,\"ck\":false,\"sp\":false},\"fuseNot\":false},\"30\":{\"termUsed\":\"-\",\"type\":\"N\",\"name\":\"R2\",\"number\":30,\"negated\":false,\"extensions\":{\"ar\":false,\"d\":false,\"ck\":false,\"sp\":false},\"fuseNot\":false},\"31\":{\"termUsed\":\"-\",\"type\":\"N\",\"name\":\"R3\",\"number\":31,\"negated\":false,\"extensions\":{\"ar\":false,\"d\":false,\"ck\":false,\"sp\":false},\"fuseNot\":false},\"32\":{\"termUsed\":\"-\",\"type\":\"N\",\"name\":\"R4\",\"number\":32,\"negated\":false,\"extensions\":{\"ar\":false,\"d\":false,\"ck\":false,\"sp\":false},\"fuseNot\":false}}}")) pld_1: pin names not known; wires that end beside it: CLK, usbport_1_p1, pld_1_p3, usbport_1_p5, usbport_1_p4, usbport_1_p3, usbport_1_p2, Sclose, Sopen, Psensor, pld_1_p3, pld_1_p12, On, pld_1_p14, pld_1_p15, pld_1_p16, pld_1_p17, pld_1_p18, pld_1_p12, pld_1_p14, pld_1_p15, pld_1_p16, pld_1_p17, pld_1_p18
endmodule
