// Logisim project KeyboardReader.circ as structural Verilog: 3 circuits, main circuit main
// TXclk
module main (
);

  wire CLK___B_out, CLK___D_out, DAC, DVal, n4x4_matrix_keyboard_1_p1, n4x4_matrix_keyboard_1_p2,
       n4x4_matrix_keyboard_1_p3, n4x4_matrix_keyboard_1_p4, n4x4_matrix_keyboard_1_p5,
       n4x4_matrix_keyboard_1_p6, n4x4_matrix_keyboard_1_p7, TXclk, TXd;
  wire [3:0] pld_1_p12;

  Clock #(.highDuration(3), .lowDuration(3)) CLK___D (.out(CLK___D_out));
  Clock CLK___B (.out(CLK___B_out));
  // _4x4_Matrix_Keyboard 4x4_matrix_keyboard_1: pin names not known; wires that end beside it: n4x4_matrix_keyboard_1_p1, n4x4_matrix_keyboard_1_p2, n4x4_matrix_keyboard_1_p3, n4x4_matrix_keyboard_1_p4, n4x4_matrix_keyboard_1_p5, n4x4_matrix_keyboard_1_p6, n4x4_matrix_keyboard_1_p7
  Pull_Resistor #(.pull(1)) pull_resistor_1 (.node(n4x4_matrix_keyboard_1_p4));
  Pull_Resistor #(.pull(1)) pull_resistor_2 (.node(n4x4_matrix_keyboard_1_p5));
  Pull_Resistor #(.pull(1)) pull_resistor_3 (.node(n4x4_matrix_keyboard_1_p6));
  Pull_Resistor #(.pull(1)) pull_resistor_4 (.node(n4x4_matrix_keyboard_1_p7));
  // PLD #(.Contents("{\"version\":\"1.0\",\"deviceId\":\"v750c\",\"file\":\"template.doc\",\"variables\":{\"Q1\":false,\"Q2\":false,\"Q0.dfb\":false,\"Q3\":false,\"CLK\":false,\"KO1\":true,\"KO0\":true,\"D1.dfb\":false,\"C0\":false,\"KO3\":true,\"C1\":false,\"KO2\":true,\"C2\":false,\"C3\":false,\"KI1\":false,\"KI0\":false,\"KI2\":false,\"D0.dfb\":false,\"T0\":false,\"T1\":false,\"C1.dfb\":false,\"T2\":false,\"T0.dfb\":false,\"ACK\":false,\"Q3.dfb\":false,\"C2.dfb\":false,\"D0\":false,\"D1\":false,\"T1.dfb\":false,\"C0.dfb\":false,\"MCLK\":false,\"Q1.dfb\":false,\"C3.dfb\":false,\"Q2.dfb\":false,\"Dval\":false,\"T2.dfb\":false,\"Q0\":false},\"productTerms\":[{\"type\":\"I\",\"pin\":0,\"result\":true,\"name\":\"A0\",\"expression\":\"!C0\\u0026!C1\"},{\"type\":\"I\",\"pin\":0,\"result\":false,\"name\":\"A1\",\"expression\":\"C0\\u0026!C1\"},{\"type\":\"I\",\"pin\":0,\"result\":false,\"name\":\"A2\",\"expression\":\"!C0\\u0026C1\"},{\"type\":\"I\",\"pin\":0,\"result\":false,\"name\":\"A3\",\"expression\":\"C0\\u0026C1\"},{\"type\":\"M\",\"pin\":28,\"result\":true,\"name\":\"C0.d\",\"expression\":\"C0\\u0026!C1\\u0026D0#C0\\u0026C2\\u0026D0#C0\\u0026!C3\\u0026D0#C0\\u0026!C1\\u0026D1#C0\\u0026C2\\u0026D1#C0\\u0026!C3\\u0026D1#!C0\\u0026!D0\\u0026!D1\"},{\"type\":\"M\",\"pin\":28,\"result\":false,\"name\":\"C0.ar\",\"expression\":\"0\"},{\"type\":\"M\",\"pin\":28,\"result\":true,\"name\":\"C0.ck\",\"expression\":\"!MCLK\"},{\"type\":\"M\",\"pin\":28,\"result\":false,\"name\":\"C0.sp\",\"expression\":\"0\"},{\"type\":\"M\",\"pin\":29,\"result\":false,\"name\":\"C1.d\",\"expression\":\"!C0\\u0026C1#C1\\u0026C2\\u0026D0#C1\\u0026!C3\\u0026D0#C1\\u0026C2\\u0026D1#C1\\u0026!C3\\u0026D1#C0\\u0026!C1\\u0026!D0\\u0026!D1\"},{\"type\":\"M\",\"pin\":29,\"result\":false,\"name\":\"C1.ar\",\"expression\":\"0\"},{\"type\":\"M\",\"pin\":29,\"result\":true,\"name\":\"C1.ck\",\"expression\":\"!MCLK\"},{\"type\":\"M\",\"pin\":29,\"result\":false,\"name\":\"C1.sp\",\"expression\":\"0\"},{\"type\":\"M\",\"pin\":30,\"result\":false,\"name\":\"C2.d\",\"expression\":\"!C0\\u0026C2#!C1\\u0026C2#C2\\u0026D0#C2\\u0026D1#C0\\u0026C1\\u0026!C2\\u0026!C3\\u0026!D0\\u0026!D1\"},{\"type\":\"M\",\"pin\":30,\"result\":false,\"name\":\"C2.ar\",\"expression\":\"0\"},{\"type\":\"M\",\"pin\":30,\"result\":true,\"name\":\"C2.ck\",\"expression\":\"!MCLK\"},{\"type\":\"M\",\"pin\":30,\"result\":false,\"name\":\"C2.sp\",\"expression\":\"0\"},{\"type\":\"M\",\"pin\":26,\"result\":false,\"name\":\"C3.d\",\"expression\":\"!C0\\u0026C3#!C1\\u0026C3#C2\\u0026C3\\u0026D0#C2\\u0026C3\\u0026D1#C0\\u0026C1\\u0026C2\\u0026!C3\\u0026!D0\\u0026!D1\"},{\"type\":\"M\",\"pin\":26,\"result\":false,\"name\":\"C3.ar\",\"expression\":\"0\"},{\"type\":\"M\",\"pin\":26,\"result\":true,\"name\":\"C3.ck\",\"expression\":\"!MCLK\"},{\"type\":\"M\",\"pin\":26,\"result\":false,\"name\":\"C3.sp\",\"expression\":\"0\"},{\"type\":\"I\",\"pin\":0,\"result\":true,\"name\":\"CE\",\"expression\":\"!D0\\u0026!D1\"},{\"type\":\"M\",\"pin\":31,\"result\":false,\"name\":\"D0.d\",\"expression\":\"D0\\u0026!D1\\u0026T0#D0\\u0026!D1\\u0026!T1#D0\\u0026!D1\\u0026T2#!C0\\u0026!C1\\u0026!D0\\u0026!D1\\u0026!KO0#C0\\u0026!C1\\u0026!D0\\u0026!D1\\u0026!KO1#!C0\\u0026C1\\u0026!D0\\u0026!D1\\u0026!KO2#C0\\u0026C1\\u0026!D0\\u0026!D1\\u0026!KO3\"},{\"type\":\"M\",\"pin\":31,\"result\":false,\"name\":\"D0.ar\",\"expression\":\"0\"},{\"type\":\"M\",\"pin\":31,\"result\":false,\"name\":\"D0.ck\",\"expression\":\"MCLK\"},{\"type\":\"M\",\"pin\":31,\"result\":false,\"name\":\"D0.sp\",\"expression\":\"0\"},{\"type\":\"M\",\"pin\":27,\"result\":false,\"name\":\"D1.d\",\"expression\":\"!C0\\u0026!C1\\u0026!D0\\u0026D1\\u0026!KO0#C0\\u0026!C1\\u0026!D0\\u0026D1\\u0026!KO1#!C0\\u0026C1\\u0026!D0\\u0026D1\\u0026!KO2#C0\\u0026C1\\u0026!D0\\u0026D1\\u0026!KO3#!D0\\u0026D1\\u0026!T0\\u0026T1\\u0026!T2#D0\\u0026!D1\\u0026!T0\\u0026T1\\u0026!T2\"},{\"type\":\"M\",\"pin\":27,\"result\":false,\"name\":\"D1.ar\",\"expression\":\"0\"},{\"type\":\"M\",\"pin\":27,\"result\":false,\"name\":\"D1.ck\",\"expression\":\"MCLK\"},{\"type\":\"M\",\"pin\":27,\"result\":false,\"name\":\"D1.sp\",\"expression\":\"0\"},{\"type\":\"I\",\"pin\":0,\"result\":false,\"name\":\"DAC\",\"expression\":\"!T0\\u0026T1\\u0026!T2\"},{\"type\":\"I\",\"pin\":0,\"result\":false,\"name\":\"DAV\",\"expression\":\"D0\\u0026!D1\"},{\"type\":\"V\",\"pin\":22,\"result\":false,\"name\":\"Dval\",\"expression\":\"T0\\u0026T1\\u0026!T2\"},{\"type\":\"I\",\"pin\":0,\"result\":false,\"name\":\"K0\",\"expression\":\"C0\"},{\"type\":\"I\",\"pin\":0,\"result\":false,\"name\":\"K1\",\"expression\":\"C1\"},{\"type\":\"I\",\"pin\":0,\"result\":false,\"name\":\"K2\",\"expression\":\"C2\"},{\"type\":\"I\",\"pin\":0,\"result\":false,\"name\":\"K3\",\"expression\":\"C3\"},{\"type\":\"V\",\"pin\":14,\"result\":false,\"name\":\"KI0\",\"expression\":\"!C2\\u0026!C3\"},{\"type\":\"V\",\"pin\":15,\"result\":true,\"name\":\"KI1\",\"expression\":\"C2\\u0026!C3\"},{\"type\":\"V\",\"pin\":16,\"result\":true,\"name\":\"KI2\",\"expression\":\"!C2\\u0026C3\"},{\"type\":\"I\",\"pin\":0,\"result\":false,\"name\":\"KPressed\",\"expression\":\"!KO0\\u0026!KO1\\u0026!KO2\\u0026!KO3#C1\\u0026!KO2\\u0026!KO3#C0\\u0026!KO1\\u0026!KO3#C0\\u0026C1\\u0026!KO3#!C0\\u0026!KO0\\u0026!KO2#!C0\\u0026C1\\u0026!KO2#!C0\\u0026!C1\\u0026!KO0#!C1\\u0026!KO0\\u0026!KO1#C0\\u0026!C1\\u0026!KO1\"},{\"type\":\"I\",\"pin\":0,\"result\":false,\"name\":\"Kack\",\"expression\":\"!T0\\u0026T1\\u0026!T2\"},{\"type\":\"I\",\"pin\":0,\"result\":true,\"name\":\"Kscan\",\"expression\":\"!D0\\u0026!D1\"},{\"type\":\"I\",\"pin\":0,\"result\":false,\"name\":\"Kval\",\"expression\":\"D0\\u0026!D1\"},{\"type\":\"X\",\"pin\":17,\"result\":false,\"name\":\"Q0.d\",\"expression\":\"C0\"},{\"type\":\"X\",\"pin\":17,\"result\":false,\"name\":\"Q0.ar\",\"expression\":\"0\"},{\"type\":\"X\",\"pin\":17,\"result\":false,\"name\":\"Q0.ck\",\"expression\":\"T0\\u0026!T1\\u0026!T2\"},{\"type\":\"X\",\"pin\":17,\"result\":false,\"name\":\"Q0.sp\",\"expression\":\"0\"},{\"type\":\"X\",\"pin\":18,\"result\":false,\"name\":\"Q1.d\",\"expression\":\"C1\"},{\"type\":\"X\",\"pin\":18,\"result\":false,\"name\":\"Q1.ar\",\"expression\":\"0\"},{\"type\":\"X\",\"pin\":18,\"result\":false,\"name\":\"Q1.ck\",\"expression\":\"T0\\u0026!T1\\u0026!T2\"},{\"type\":\"X\",\"pin\":18,\"result\":false,\"name\":\"Q1.sp\",\"expression\":\"0\"},{\"type\":\"X\",\"pin\":19,\"result\":false,\"name\":\"Q2.d\",\"expression\":\"C2\"},{\"type\":\"X\",\"pin\":19,\"result\":false,\"name\":\"Q2.ar\",\"expression\":\"0\"},{\"type\":\"X\",\"pin\":19,\"result\":false,\"name\":\"Q2.ck\",\"expression\":\"T0\\u0026!T1\\u0026!T2\"},{\"type\":\"X\",\"pin\":19,\"result\":false,\"name\":\"Q2.sp\",\"expression\":\"0\"},{\"type\":\"X\",\"pin\":20,\"result\":false,\"name\":\"Q3.d\",\"expression\":\"C3\"},{\"type\":\"X\",\"pin\":20,\"result\":false,\"name\":\"Q3.ar\",\"expression\":\"0\"},{\"type\":\"X\",\"pin\":20,\"result\":false,\"name\":\"Q3.ck\",\"expression\":\"T0\\u0026!T1\\u0026!T2\"},{\"type\":\"X\",\"pin\":20,\"result\":false,\"name\":\"Q3.sp\",\"expression\":\"0\"},{\"type\":\"I\",\"pin\":0,\"result\":true,\"name\":\"R\",\"expression\":\"!C0#!C1#C2#!C3\"},{\"type\":\"M\",\"pin\":32,\"result\":false,\"name\":\"T0.d\",\"expression\":\"!ACK\\u0026T0\\u0026T1\\u0026!T2#!D0\\u0026!T0\\u0026T1\\u0026!T2#D1\\u0026!T0\\u0026T1\\u0026!T2#D0\\u0026!D1\\u0026!T0\\u0026!T1\\u0026!T2\"},{\"type\":\"M\",\"pin\":32,\"result\":false,\"name\":\"T0.ar\",\"expression\":\"0\"},{\"type\":\"M\",\"pin\":32,\"result\":false,\"name\":\"T0.ck\",\"expression\":\"CLK\"},{\"type\":\"M\",\"pin\":32,\"result\":false,\"name\":\"T0.sp\",\"expression\":\"0\"},{\"type\":\"M\",\"pin\":33,\"result\":false,\"name\":\"T1.d\",\"expression\":\"!ACK\\u0026T0\\u0026!T2#!T0\\u0026T1\\u0026!T2#T0\\u0026!T1\\u0026!T2\"},{\"type\":\"M\",\"pin\":33,\"result\":false,\"name\":\"T1.ar\",\"expression\":\"0\"},{\"type\":\"M\",\"pin\":33,\"result\":false,\"name\":\"T1.ck\",\"expression\":\"CLK\"},{\"type\":\"M\",\"pin\":33,\"result\":false,\"name\":\"T1.sp\",\"expression\":\"0\"},{\"type\":\"M\",\"pin\":34,\"result\":false,\"name\":\"T2.d\",\"expression\":\"ACK\\u0026!T0\\u0026!T1\\u0026T2#ACK\\u0026T0\\u0026T1\\u0026!T2\"},{\"type\":\"M\",\"pin\":34,\"result\":false,\"name\":\"T2.ar\",\"expression\":\"0\"},{\"type\":\"M\",\"pin\":34,\"result\":false,\"name\":\"T2.ck\",\"expression\":\"CLK\"},{\"type\":\"M\",\"pin\":34,\"result\":false,\"name\":\"T2.sp\",\"expression\":\"0\"},{\"type\":\"I\",\"pin\":0,\"result\":false,\"name\":\"Wreg\",\"expression\":\"T0\\u0026!T1\\u0026!T2\"},{\"type\":\"D\",\"pin\":22,\"result\":true,\"name\":\"Dval.oe\",\"expression\":\"1\"},{\"type\":\"D\",\"pin\":14,\"result\":true,\"name\":\"KI0.oe\",\"expression\":\"1\"},{\"type\":\"D\",\"pin\":15,\"result\":true,\"name\":\"KI1.oe\",\"expression\":\"1\"},{\"type\":\"D\",\"pin\":16,\"result\":true,\"name\":\"KI2.oe\",\"expression\":\"1\"},{\"type\":\"D\",\"pin\":17,\"result\":true,\"name\":\"Q0.oe\",\"expression\":\"1\"},{\"type\":\"D\",\"pin\":18,\"result\":true,\"name\":\"Q1.oe\",\"expression\":\"1\"},{\"type\":\"D\",\"pin\":19,\"result\":true,\"name\":\"Q2.oe\",\"expression\":\"1\"},{\"type\":\"D\",\"pin\":20,\"result\":true,\"name\":\"Q3.oe\",\"expression\":\"1\"}],\"projectName\":\"template\",\"pins\":{\"32\":{\"termUsed\":\"-\",\"type\":\"N\",\"name\":\"T0\",\"number\":32,\"negated\":false,\"extensions\":{\"ar\":false,\"d\":false,\"ck\":false,\"sp\":false},\"fuseNot\":false},\"1\":{\"termUsed\":\"-\",\"type\":\"V\",\"name\":\"MCLK\",\"number\":1,\"negated\":false,\"extensions\":{},\"fuseNot\":false},\"33\":{\"termUsed\":\"-\",\"type\":\"N\",\"name\":\"T1\",\"number\":33,\"negated\":false,\"extensions\":{\"ar\":false,\"d\":false,\"ck\":false,\"sp\":false},\"fuseNot\":false},\"2\":{\"termUsed\":\"-\",\"type\":\"V\",\"name\":\"CLK\",\"number\":2,\"negated\":false,\"extensions\":{},\"fuseNot\":false},\"34\":{\"termUsed\":\"-\",\"type\":\"N\",\"name\":\"T2\",\"number\":34,\"negated\":false,\"extensions\":{\"ar\":false,\"d\":false,\"ck\":false,\"sp\":false},\"fuseNot\":false},\"3\":{\"termUsed\":\"-\",\"type\":\"V\",\"name\":\"KO0\",\"number\":3,\"negated\":false,\"extensions\":{},\"fuseNot\":false},\"4\":{\"termUsed\":\"-\",\"type\":\"V\",\"name\":\"KO1\",\"number\":4,\"negated\":false,\"extensions\":{},\"fuseNot\":false},\"5\":{\"termUsed\":\"-\",\"type\":\"V\",\"name\":\"KO2\",\"number\":5,\"negated\":false,\"extensions\":{},\"fuseNot\":false},\"6\":{\"termUsed\":\"-\",\"type\":\"V\",\"name\":\"KO3\",\"number\":6,\"negated\":false,\"extensions\":{},\"fuseNot\":false},\"7\":{\"termUsed\":\"-\",\"type\":\"V\",\"name\":\"ACK\",\"number\":7,\"negated\":false,\"extensions\":{},\"fuseNot\":false},\"14\":{\"termUsed\":\"1\",\"type\":\"V\",\"name\":\"KI0\",\"number\":14,\"negated\":false,\"extensions\":{\"oe\":true,\"value\":false},\"fuseNot\":true},\"15\":{\"termUsed\":\"1\",\"type\":\"V\",\"name\":\"KI1\",\"number\":15,\"negated\":false,\"extensions\":{\"oe\":true,\"value\":true},\"fuseNot\":true},\"16\":{\"termUsed\":\"1\",\"type\":\"V\",\"name\":\"KI2\",\"number\":16,\"negated\":false,\"extensions\":{\"oe\":true,\"value\":true},\"fuseNot\":true},\"17\":{\"termUsed\":\"-\",\"type\":\"V\",\"name\":\"Q0\",\"number\":17,\"negated\":false,\"extensions\":{\"ar\":false,\"d\":false,\"oe\":true,\"ck\":false,\"sp\":false},\"fuseNot\":false},\"18\":{\"termUsed\":\"-\",\"type\":\"V\",\"name\":\"Q1\",\"number\":18,\"negated\":false,\"extensions\":{\"ar\":false,\"d\":false,\"oe\":true,\"ck\":false,\"sp\":false},\"fuseNot\":false},\"19\":{\"termUsed\":\"-\",\"type\":\"V\",\"name\":\"Q2\",\"number\":19,\"negated\":false,\"extensions\":{\"ar\":false,\"d\":false,\"oe\":true,\"ck\":false,\"sp\":false},\"fuseNot\":false},\"20\":{\"termUsed\":\"-\",\"type\":\"V\",\"name\":\"Q3\",\"number\":20,\"negated\":false,\"extensions\":{\"ar\":false,\"d\":false,\"oe\":true,\"ck\":false,\"sp\":false},\"fuseNot\":false},\"22\":{\"termUsed\":\"1\",\"type\":\"V\",\"name\":\"Dval\",\"number\":22,\"negated\":false,\"extensions\":{\"oe\":true,\"value\":false},\"fuseNot\":false},\"26\":{\"termUsed\":\"-\",\"type\":\"N\",\"name\":\"C3\",\"number\":26,\"negated\":false,\"extensions\":{\"ar\":false,\"d\":false,\"ck\":true,\"sp\":false},\"fuseNot\":false},\"27\":{\"termUsed\":\"-\",\"type\":\"N\",\"name\":\"D1\",\"number\":27,\"negated\":false,\"extensions\":{\"ar\":false,\"d\":false,\"ck\":false,\"sp\":false},\"fuseNot\":false},\"28\":{\"termUsed\":\"-\",\"type\":\"N\",\"name\":\"C0\",\"number\":28,\"negated\":false,\"extensions\":{\"ar\":false,\"d\":false,\"ck\":true,\"sp\":false},\"fuseNot\":false},\"29\":{\"termUsed\":\"-\",\"type\":\"N\",\"name\":\"C1\",\"number\":29,\"negated\":false,\"extensions\":{\"ar\":false,\"d\":true,\"ck\":true,\"sp\":false},\"fuseNot\":false},\"30\":{\"termUsed\":\"-\",\"type\":\"N\",\"name\":\"C2\",\"number\":30,\"negated\":false,\"extensions\":{\"ar\":false,\"d\":false,\"ck\":true,\"sp\":false},\"fuseNot\":false},\"31\":{\"termUsed\":\"-\",\"type\":\"N\",\"name\":\"D0\",\"number\":31,\"negated\":false,\"extensions\":{\"ar\":false,\"d\":false,\"ck\":false,\"sp\":false},\"fuseNot\":false}}}")) pld_1: pin names not known; wires that end beside it: CLK___D_out, CLK___B_out, n4x4_matrix_keyboard_1_p4, n4x4_matrix_keyboard_1_p5, n4x4_matrix_keyboard_1_p6, n4x4_matrix_keyboard_1_p7, DAC, DVal, pld_1_p12[3], pld_1_p12[2], pld_1_p12[1], pld_1_p12[0], n4x4_matrix_keyboard_1_p3, n4x4_matrix_keyboard_1_p2, n4x4_matrix_keyboard_1_p1
  // UsbPort usbport_1: pin names not known; wires that end beside it: TXclk, TXd
  // PLD #(.Contents("{\"version\":\"1.0\",\"deviceId\":\"v750c\",\"file\":\"template.doc\",\"variables\":{\"Q1\":false,\"K0.dfb\":false,\"Q2\":false,\"Q0.dfb\":false,\"K0\":false,\"K1\":false,\"K2\":false,\"K3\":false,\"TXclk\":false,\"K3.dfb\":false,\"T0\":false,\"T1\":false,\"T2\":false,\"T0.dfb\":false,\"TXd\":false,\"DAC\":false,\"K2.dfb\":false,\"D0\":false,\"D1\":false,\"D2\":false,\"D3\":false,\"T1.dfb\":false,\"MCLK\":false,\"Q1.dfb\":false,\"DAV\":false,\"K1.dfb\":false,\"Q2.dfb\":false,\"T2.dfb\":false,\"Q0\":false},\"productTerms\":[{\"type\":\"I\",\"pin\":0,\"result\":false,\"name\":\"C1\",\"expression\":\"Q0\\u0026!Q1\\u0026!Q2\"},{\"type\":\"I\",\"pin\":0,\"result\":false,\"name\":\"C2\",\"expression\":\"!Q0\\u0026Q1\\u0026!Q2\"},{\"type\":\"I\",\"pin\":0,\"result\":false,\"name\":\"C3\",\"expression\":\"Q0\\u0026Q1\\u0026!Q2\"},{\"type\":\"I\",\"pin\":0,\"result\":false,\"name\":\"C4\",\"expression\":\"!Q0\\u0026!Q1\\u0026Q2\"},{\"type\":\"I\",\"pin\":0,\"result\":false,\"name\":\"C5\",\"expression\":\"Q0\\u0026!Q1\\u0026Q2\"},{\"type\":\"I\",\"pin\":0,\"result\":false,\"name\":\"CE\",\"expression\":\"T2#T0\\u0026T1\"},{\"type\":\"V\",\"pin\":14,\"result\":false,\"name\":\"DAC\",\"expression\":\"!T0\\u0026T1\\u0026!T2\"},{\"type\":\"I\",\"pin\":0,\"result\":false,\"name\":\"END\",\"expression\":\"Q0\\u0026Q1\\u0026Q2\"},{\"type\":\"M\",\"pin\":20,\"result\":false,\"name\":\"K0.d\",\"expression\":\"D0\"},{\"type\":\"M\",\"pin\":20,\"result\":false,\"name\":\"K0.ar\",\"expression\":\"0\"},{\"type\":\"M\",\"pin\":20,\"result\":false,\"name\":\"K0.ck\",\"expression\":\"T0\\u0026!T1\\u0026!T2\"},{\"type\":\"M\",\"pin\":20,\"result\":false,\"name\":\"K0.sp\",\"expression\":\"0\"},{\"type\":\"M\",\"pin\":21,\"result\":false,\"name\":\"K1.d\",\"expression\":\"D1\"},{\"type\":\"M\",\"pin\":21,\"result\":false,\"name\":\"K1.ar\",\"expression\":\"0\"},{\"type\":\"M\",\"pin\":21,\"result\":false,\"name\":\"K1.ck\",\"expression\":\"T0\\u0026!T1\\u0026!T2\"},{\"type\":\"M\",\"pin\":21,\"result\":false,\"name\":\"K1.sp\",\"expression\":\"0\"},{\"type\":\"M\",\"pin\":22,\"result\":false,\"name\":\"K2.d\",\"expression\":\"D2\"},{\"type\":\"M\",\"pin\":22,\"result\":false,\"name\":\"K2.ar\",\"expression\":\"0\"},{\"type\":\"M\",\"pin\":22,\"result\":false,\"name\":\"K2.ck\",\"expression\":\"T0\\u0026!T1\\u0026!T2\"},{\"type\":\"M\",\"pin\":22,\"result\":false,\"name\":\"K2.sp\",\"expression\":\"0\"},{\"type\":\"M\",\"pin\":23,\"result\":false,\"name\":\"K3.d\",\"expression\":\"D3\"},{\"type\":\"M\",\"pin\":23,\"result\":false,\"name\":\"K3.ar\",\"expression\":\"0\"},{\"type\":\"M\",\"pin\":23,\"result\":false,\"name\":\"K3.ck\",\"expression\":\"T0\\u0026!T1\\u0026!T2\"},{\"type\":\"M\",\"pin\":23,\"result\":false,\"name\":\"K3.sp\",\"expression\":\"0\"},{\"type\":\"I\",\"pin\":0,\"result\":false,\"name\":\"ON\",\"expression\":\"T0\\u0026T1\\u0026!T2#!T0\\u0026!T1\\u0026T2\"},{\"type\":\"M\",\"pin\":27,\"result\":false,\"name\":\"Q0.t\",\"expression\":\"T2#T0\\u0026T1\"},{\"type\":\"M\",\"pin\":27,\"result\":false,\"name\":\"Q0.ar\",\"expression\":\"T0\\u0026T1\\u0026!T2\"},{\"type\":\"M\",\"pin\":27,\"result\":false,\"name\":\"Q0.ck\",\"expression\":\"TXclk\"},{\"type\":\"M\",\"pin\":27,\"result\":false,\"name\":\"Q0.sp\",\"expression\":\"0\"},{\"type\":\"M\",\"pin\":28,\"result\":false,\"name\":\"Q1.t\",\"expression\":\"Q0\\u0026T2#Q0\\u0026T0\\u0026T1\"},{\"type\":\"M\",\"pin\":28,\"name\":\"Q1.ar\",\"expression\":\"T0\\u0026T1\\u0026!T2\"},{\"type\":\"M\",\"pin\":28,\"result\":false,\"name\":\"Q1.ck\",\"expression\":\"TXclk\"},{\"type\":\"M\",\"pin\":28,\"result\":false,\"name\":\"Q1.sp\",\"expression\":\"0\"},{\"type\":\"M\",\"pin\":29,\"result\":false,\"name\":\"Q2.t\",\"expression\":\"Q0\\u0026Q1\\u0026T2#Q0\\u0026Q1\\u0026T0\\u0026T1\"},{\"type\":\"M\",\"pin\":29,\"result\":false,\"name\":\"Q2.ar\",\"expression\":\"T0\\u0026T1\\u0026!T2\"},{\"type\":\"M\",\"pin\":29,\"result\":false,\"name\":\"Q2.ck\",\"expression\":\"TXclk\"},{\"type\":\"M\",\"pin\":29,\"result\":false,\"name\":\"Q2.sp\",\"expression\":\"0\"},{\"type\":\"I\",\"pin\":0,\"result\":false,\"name\":\"Reset\",\"expression\":\"T0\\u0026T1\\u0026!T2\"},{\"type\":\"X\",\"pin\":16,\"name\":\"T0.d\",\"expression\":\"!DAV\\u0026!T0\\u0026T1\\u0026!T2#DAV\\u0026!T0\\u0026!T1\\u0026!T2\"},{\"type\":\"X\",\"pin\":16,\"name\":\"T0.ar\",\"expression\":\"0\"},{\"type\":\"X\",\"pin\":16,\"name\":\"T0.ck\",\"expression\":\"MCLK\"},{\"type\":\"X\",\"pin\":16,\"name\":\"T0.sp\",\"expression\":\"0\"},{\"type\":\"X\",\"pin\":17,\"name\":\"T1.d\",\"expression\":\"!T0\\u0026T1\\u0026!T2#T0\\u0026!T1\\u0026!T2\"},{\"type\":\"X\",\"pin\":17,\"name\":\"T1.ar\",\"expression\":\"0\"},{\"type\":\"X\",\"pin\":17,\"name\":\"T1.ck\",\"expression\":\"MCLK\"},{\"type\":\"X\",\"pin\":17,\"name\":\"T1.sp\",\"expression\":\"0\"},{\"type\":\"X\",\"pin\":18,\"name\":\"T2.d\",\"expression\":\"T0\\u0026T1\\u0026!T2#!Q0\\u0026!T0\\u0026!T1\\u0026T2#!Q1\\u0026!T0\\u0026!T1\\u0026T2#!Q2\\u0026!T0\\u0026!T1\\u0026T2\"},{\"type\":\"X\",\"pin\":18,\"name\":\"T2.ar\",\"expression\":\"0\"},{\"type\":\"X\",\"pin\":18,\"name\":\"T2.ck\",\"expression\":\"MCLK\"},{\"type\":\"X\",\"pin\":18,\"name\":\"T2.sp\",\"expression\":\"0\"},{\"type\":\"V\",\"pin\":15,\"name\":\"TXd\",\"expression\":\"!T0\\u0026T1#T0\\u0026T2#!T1\\u0026!T2#K3\\u0026Q0\\u0026!Q1#K1\\u0026Q0\\u0026!Q2#Q0\\u0026!Q1\\u0026!Q2#K2\\u0026!Q0\\u0026!Q1\\u0026Q2#K0\\u0026!Q0\\u0026Q1\\u0026!Q2\"},{\"type\":\"I\",\"pin\":0,\"name\":\"Wr\",\"expression\":\"T0\\u0026!T1\\u0026!T2\"},{\"type\":\"D\",\"pin\":14,\"name\":\"DAC.oe\",\"expression\":\"1\"},{\"type\":\"D\",\"pin\":20,\"name\":\"K0.oe\",\"expression\":\"1\"},{\"type\":\"D\",\"pin\":21,\"name\":\"K1.oe\",\"expression\":\"1\"},{\"type\":\"D\",\"pin\":22,\"name\":\"K2.oe\",\"expression\":\"1\"},{\"type\":\"D\",\"pin\":23,\"name\":\"K3.oe\",\"expression\":\"1\"},{\"type\":\"D\",\"pin\":16,\"name\":\"T0.oe\",\"expression\":\"1\"},{\"type\":\"D\",\"pin\":17,\"name\":\"T1.oe\",\"expression\":\"1\"},{\"type\":\"D\",\"pin\":18,\"name\":\"T2.oe\",\"expression\":\"1\"},{\"type\":\"D\",\"pin\":15,\"name\":\"TXd.oe\",\"expression\":\"1\"}],\"projectName\":\"template\",\"pins\":{\"1\":{\"termUsed\":\"-\",\"type\":\"V\",\"name\":\"MCLK\",\"number\":1,\"negated\":false,\"extensions\":{},\"fuseNot\":false},\"2\":{\"termUsed\":\"-\",\"type\":\"V\",\"name\":\"DAV\",\"number\":2,\"negated\":false,\"extensions\":{},\"fuseNot\":false},\"3\":{\"termUsed\":\"-\",\"type\":\"V\",\"name\":\"D0\",\"number\":3,\"negated\":false,\"extensions\":{},\"fuseNot\":false},\"4\":{\"termUsed\":\"-\",\"type\":\"V\",\"name\":\"D1\",\"number\":4,\"negated\":false,\"extensions\":{},\"fuseNot\":false},\"5\":{\"termUsed\":\"-\",\"type\":\"V\",\"name\":\"D2\",\"number\":5,\"negated\":false,\"extensions\":{},\"fuseNot\":false},\"6\":{\"termUsed\":\"-\",\"type\":\"V\",\"name\":\"D3\",\"number\":6,\"negated\":false,\"extensions\":{},\"fuseNot\":false},\"7\":{\"termUsed\":\"-\",\"type\":\"V\",\"name\":\"TXclk\",\"number\":7,\"negated\":false,\"extensions\":{},\"fuseNot\":false},\"14\":{\"termUsed\":\"1\",\"type\":\"V\",\"name\":\"DAC\",\"number\":14,\"negated\":false,\"extensions\":{\"oe\":true,\"value\":false},\"fuseNot\":false},\"15\":{\"termUsed\":\"8\",\"type\":\"V\",\"name\":\"TXd\",\"number\":15,\"negated\":false,\"extensions\":{\"oe\":true,\"value\":true},\"fuseNot\":false},\"16\":{\"termUsed\":\"-\",\"type\":\"V\",\"name\":\"T0\",\"number\":16,\"negated\":false,\"extensions\":{\"ar\":false,\"d\":false,\"oe\":true,\"ck\":false,\"sp\":false},\"fuseNot\":false},\"17\":{\"termUsed\":\"-\",\"type\":\"V\",\"name\":\"T1\",\"number\":17,\"negated\":false,\"extensions\":{\"ar\":false,\"d\":false,\"oe\":true,\"ck\":false,\"sp\":false},\"fuseNot\":false},\"18\":{\"termUsed\":\"-\",\"type\":\"V\",\"name\":\"T2\",\"number\":18,\"negated\":false,\"extensions\":{\"ar\":false,\"d\":false,\"oe\":true,\"ck\":false,\"sp\":false},\"fuseNot\":false},\"20\":{\"termUsed\":\"-\",\"type\":\"N\",\"name\":\"K0\",\"number\":20,\"negated\":false,\"extensions\":{\"ar\":false,\"d\":false,\"oe\":true,\"ck\":false,\"sp\":false},\"fuseNot\":false},\"21\":{\"termUsed\":\"-\",\"type\":\"N\",\"name\":\"K1\",\"number\":21,\"negated\":false,\"extensions\":{\"ar\":false,\"d\":false,\"oe\":true,\"ck\":false,\"sp\":false},\"fuseNot\":false},\"22\":{\"termUsed\":\"-\",\"type\":\"N\",\"name\":\"K2\",\"number\":22,\"negated\":false,\"extensions\":{\"ar\":false,\"d\":false,\"oe\":true,\"ck\":false,\"sp\":false},\"fuseNot\":false},\"23\":{\"termUsed\":\"-\",\"type\":\"N\",\"name\":\"K3\",\"number\":23,\"negated\":false,\"extensions\":{\"ar\":false,\"d\":false,\"oe\":true,\"ck\":false,\"sp\":false},\"fuseNot\":false},\"27\":{\"termUsed\":\"-\",\"type\":\"N\",\"name\":\"Q0\",\"number\":27,\"negated\":false,\"extensions\":{\"ar\":false,\"t\":false,\"ck\":false,\"sp\":false},\"fuseNot\":false},\"28\":{\"termUsed\":\"-\",\"type\":\"N\",\"name\":\"Q1\",\"number\":28,\"negated\":false,\"extensions\":{\"ar\":false,\"t\":false,\"ck\":false,\"sp\":false},\"fuseNot\":false},\"29\":{\"termUsed\":\"-\",\"type\":\"N\",\"name\":\"Q2\",\"number\":29,\"negated\":false,\"extensions\":{\"ar\":false,\"t\":false,\"ck\":false,\"sp\":false},\"fuseNot\":false}}}")) pld_2: pin names not known; wires that end beside it: CLK___D_out, DVal, pld_1_p12[0], pld_1_p12[1], pld_1_p12[2], pld_1_p12[3], TXclk, TXd, DAC
endmodule

module Buffer (
  input  in_1,
  input  DAV,
  input  ACK,
  output Wreg,
  output Dval,
  output DAC
);

  wire and_1_out, and_2_out, multiplexer_1_out, multiplexer_2_out;
  wire [1:0] d_ff_1_q;

  and and_1 (and_1_out, DAV, ACK);
  Multiplexer #(.select(2), .enable("false")) multiplexer_1 (
    .in0(and_1_out), .in1(1'b0), .in2(ACK), .in3(1'b0), .out(multiplexer_1_out), .sel(d_ff_1_q));
  Multiplexer #(.select(2), .enable("false")) multiplexer_2 (
    .in0(1'b0), .in1(1'b1), .in2(1'b1), .in3(1'b0), .out(multiplexer_2_out), .sel(d_ff_1_q));
  D_Flip_Flop d_ff_1 (.clk(in_1), .D(multiplexer_1_out), .Q(d_ff_1_q[0]));  // open: Qn, preset, en, reset
  D_Flip_Flop d_ff_2 (.clk(in_1), .D(multiplexer_2_out), .Q(d_ff_1_q[1]));  // open: Qn, preset, en, reset
  and and_2 (and_2_out, ~d_ff_1_q[0], ~d_ff_1_q[1]);  // AND_Gate
  and and_3 (Wreg, d_ff_1_q[0], ~d_ff_1_q[1]);  // AND_Gate
  and and_4 (Dval, ~d_ff_1_q[0], d_ff_1_q[1]);  // AND_Gate
  and and_5 (DAC, d_ff_1_q[0], d_ff_1_q[1]);
endmodule

module register (
  input  in_1,
  input  in_2,
  input  in_3,
  input  in_4,
  input  in_5,
  output out_6,
  output out_7,
  output out_8,
  output out_9
);

  D_Flip_Flop d_ff_1 (.clk(in_1), .D(in_2), .Q(out_6));  // open: Qn, preset, en, reset
  D_Flip_Flop d_ff_2 (.clk(in_1), .D(in_3), .Q(out_7));  // open: Qn, preset, en, reset
  D_Flip_Flop d_ff_3 (.clk(in_1), .D(in_4), .Q(out_8));  // open: Qn, preset, en, reset
  D_Flip_Flop d_ff_4 (.clk(in_1), .D(in_5), .Q(out_9));  // open: Qn, preset, en, reset
endmodule
