// Logisim project KeyboardTransmitter.circ as structural Verilog: 1 circuit, main circuit main
module main (
  input  ON,
  input  TXclk,
  input  Reset,
  input  [3:0] Q0_3,
  input  Wr,
  output TXd,
  output END_v1_0,
  output END_v2_0
);

  wire multiplexer_1_out;
  wire [2:0] counter_1_q;
  wire [3:0] K0_3;

  Multiplexer #(.select(3), .enable("false")) multiplexer_1 (
    .in0(1'b0), .in1(1'b1), .in2(K0_3[0]), .in3(K0_3[1]), .in4(K0_3[2]), .in5(K0_3[3]), .in6(1'b0),
    .in7(1'b0), .out(multiplexer_1_out), .sel(counter_1_q));
  Counter #(.width(3), .max('h7)) counter_1 (
    .Q(counter_1_q), .carry(END_v1_0), .clk(TXclk), .clr(Reset));  // open: load, D, count
  Register #(.width(4)) register_1 (.D(Q0_3), .Q(K0_3), .clk(Wr));  // open: en, clr
  and and_1 (END_v2_0, counter_1_q[0], counter_1_q[1], counter_1_q[2]);
  or or_1 (TXd, multiplexer_1_out, ~ON);  // OR_Gate
endmodule
