// Logisim project LSD (INCOMPLETO).circ as structural Verilog: 1 circuit, main circuit main
module main (
);

  // LCD_16x2 lcd_16x2_1: pin names not known
  // UsbPort usbport_1: pin names not known
  // uLICx ulicx_1: pin names not known
  // uLICx ulicx_2: pin names not known
endmodule
