// Logisim project LSD.circ as structural Verilog: 1 circuit, main circuit main
module main (
);

  wire usbport_1_p2, usbport_1_p5;
  wire [3:0] usbport_1_p1;

  // LCD_16x2 lcd_16x2_1: pin names not known; wires that end beside it: usbport_1_p1[3], usbport_1_p1[2], usbport_1_p1[1]
  // UsbPort usbport_1: pin names not known; wires that end beside it: usbport_1_p1[0], usbport_1_p2, 1'b0, usbport_1_p2, usbport_1_p5, usbport_1_p5, usbport_1_p1[3], usbport_1_p1[2], 1'b1, usbport_1_p1[1], usbport_1_p1[0], 1'b0
endmodule
